// Logisim project reg.circ as structural Verilog: 2 circuits, main circuit Sub_Register
module Sub_Register (
  input  clock_1,
  input  [7:0] in_1,
  output [7:0] out_1
);

  D_Flip_Flop d_ff_1 (.D(in_1[0]), .clk(clock_1), .Q(out_1[0]));  // open: Qn, preset, reset
  D_Flip_Flop d_ff_2 (.D(in_1[1]), .clk(clock_1), .Q(out_1[1]));  // open: Qn, preset, reset
  D_Flip_Flop d_ff_3 (.D(in_1[2]), .clk(clock_1), .Q(out_1[2]));  // open: Qn, preset, reset
  D_Flip_Flop d_ff_4 (.D(in_1[3]), .clk(clock_1), .Q(out_1[3]));  // open: Qn, preset, reset
  D_Flip_Flop d_ff_5 (.D(in_1[4]), .clk(clock_1), .Q(out_1[4]));  // open: Qn, preset, reset
  D_Flip_Flop d_ff_6 (.D(in_1[5]), .clk(clock_1), .Q(out_1[5]));  // open: Qn, preset, reset
  D_Flip_Flop d_ff_7 (.D(in_1[6]), .clk(clock_1), .Q(out_1[6]));  // open: Qn, preset, reset
  D_Flip_Flop d_ff_8 (.D(in_1[7]), .clk(clock_1), .Q(out_1[7]));  // open: Qn, preset, reset
endmodule

module FourInputRegister (
  input  [7:0] data_in,
  input  [1:0] in_2,
  output [7:0] data_out
);

  wire clock_2_out;
  wire [7:0] adder_1_out, multiplexer_1_out;

  Adder adder_1 (.a(8'h1), .b(data_out), .out(adder_1_out));  // open: cin, cout
  Clock clock_2 (.out(clock_2_out));
  Multiplexer #(.enable("false"), .select(2), .width(8)) multiplexer_1 (
    .in0(data_in), .in1({8{1'b0}}), .in2(adder_1_out), .in3(data_out), .out(multiplexer_1_out), .sel(in_2));
  Sub_Register sub_register_1 (.clock_1(clock_2_out), .in_1(multiplexer_1_out), .out_1(data_out));

  // Notes on the sheet:
  //   8-bit constant 0
  //   8-bit constant 1
endmodule
